# Fritzing sketch 3 (saved by Fritzing 0.9.4)

parts:
  元件1 = Arduino Mega 2560 (Rev3)
  J1 = Basic Servo
  hc-sr1 = hc-sr04

nets:
  5V: 元件1.5V, hc-sr1.VCC
  GND: 元件1.GND, hc-sr1.GND
  N1: 元件1.D22, hc-sr1.Echo
  N2: 元件1.D23, hc-sr1.Trig
  N3: 元件1.D25, J1.pulse
