# Fritzing sketch 6 (saved by Fritzing 0.9.3b)

parts:
  元件1 = Arduino Mega 2560 (Rev3)
  元件2 = Bluetooth HC-05 Macho

nets:
  N1: 元件1.D15/RX3, 元件2.TXD
  N2: 元件1.D14/TX3, 元件2.RXD
  5V: 元件1.5V, 元件2.VCC
  GND: 元件1.GND, 元件2.GND
